// Logisim project Adder-Subtractor.circ as structural Verilog: 6 circuits, main circuit 4-bit ADDER/SUBTRACTOR 
module _4_bit_ADDER_SUBTRACTOR (
  input  MODE,
  input  UNSIGNED,
  input  A0,
  input  B0,
  input  A1,
  input  B1,
  input  A2,
  input  B2,
  input  A3,
  input  B3,
  output out_11,
  output out_12,
  output out_13,
  output out_14,
  output [4:0] OUTPUT
);

  wire adder_1_cout, adder_2_cout, adder_3_cout, adder_4_cout, and_1_out, and_2_out, and_3_out, and_4_out,
       multiplexer_1_out, n2_s_comp_segment_1_carry_changer, n2_s_comp_segment_1_f, not_1_out, or_1_out,
       segment_1_a, segment_1_b, segment_1_c, segment_1_d, segment_1_e, segment_1_f, segment_1_g,
       ten_s_segment_1_a, ten_s_segment_1_b_2, ten_s_segment_1_c_2, ten_s_segment_1_d_2, ten_s_segment_1_e_2,
       ten_s_segment_1_f, ten_s_segment_1_g, xor_1_out, xor_2_out, xor_3_out, xor_4_out, xor_5_out;
  wire [4:0] multiplexer_3_out, negator_1_f;

  _2_S_COMP_SEGMENT u_2_s_comp_segment_1 (
    ._2_S_COMP(MODE), .UNSIGNED(UNSIGNED), .F(n2_s_comp_segment_1_f),
    .CARRY_CHANGER(n2_s_comp_segment_1_carry_changer));
  Multiplexer #(.enable("false")) multiplexer_1 (
    .in0(1'b0), .in1(1'b1), .out(multiplexer_1_out), .sel(n2_s_comp_segment_1_f));
  LED #(.active("false")) ADDITION (.in(multiplexer_1_out));
  LED SUBTRACTION (.in(multiplexer_1_out));
  LED u_B3 (.in(B3));
  LED u_B2 (.in(B2));
  xor xor_1 (xor_1_out, multiplexer_1_out, B0);
  xor xor_2 (xor_2_out, multiplexer_1_out, B1);
  xor xor_3 (xor_3_out, multiplexer_1_out, B2);
  xor xor_4 (xor_4_out, multiplexer_1_out, B3);
  LED u_B0 (.in(B0));
  LED u_B1 (.in(B1));
  Adder #(.width(1)) adder_1 (.a(A0), .b(xor_1_out), .out(OUTPUT[0]), .cin(multiplexer_1_out), .cout(adder_1_cout));
  Adder #(.width(1)) adder_2 (.a(A1), .b(xor_2_out), .out(OUTPUT[1]), .cin(adder_1_cout), .cout(adder_2_cout));
  Adder #(.width(1)) adder_3 (.a(A2), .b(xor_3_out), .out(OUTPUT[2]), .cin(adder_2_cout), .cout(adder_3_cout));
  Adder #(.width(1)) adder_4 (.a(A3), .b(xor_4_out), .out(OUTPUT[3]), .cin(adder_3_cout), .cout(adder_4_cout));
  not not_1 (not_1_out, adder_4_cout);
  LED u_A3 (.in(A3));
  LED u_A2 (.in(A2));
  xor xor_5 (xor_5_out, multiplexer_1_out, B3);
  and and_1 (and_1_out, xor_5_out, not_1_out);
  and and_2 (and_2_out, xor_5_out, A3);
  and and_3 (and_3_out, not_1_out, A3);
  LED u_A0 (.in(A0));
  LED u_A1 (.in(A1));
  _2_4_DECODER u_2_4_decoder_1 (
    .A(OUTPUT[0]), .B(OUTPUT[1]), .out_3(out_11), .out_4(out_12), .out_5(out_13), .out_6(out_14));
  LED S4 (.in(OUTPUT[4]));
  Multiplexer #(.enable("false")) multiplexer_2 (
    .in0(adder_4_cout), .in1(or_1_out), .out(OUTPUT[4]), .sel(n2_s_comp_segment_1_carry_changer));
  or or_1 (or_1_out, and_1_out, and_2_out, and_3_out);
  LED S2 (.in(OUTPUT[2]));
  LED S3 (.in(OUTPUT[3]));
  LED S0 (.in(OUTPUT[0]));
  LED S1 (.in(OUTPUT[1]));
  negator negator_1 (.in_1(OUTPUT), .F(negator_1_f));
  Multiplexer #(.width(5), .enable("false")) multiplexer_3 (
    .in0(negator_1_f), .in1(OUTPUT), .out(multiplexer_3_out), .sel(UNSIGNED));
  segment segment_1 (
    .A0(multiplexer_3_out[0]), .A1(multiplexer_3_out[1]), .A2(multiplexer_3_out[2]),
    .A3(multiplexer_3_out[3]), .A4(multiplexer_3_out[4]), .a(segment_1_a), .b(segment_1_b), .c(segment_1_c),
    .d(segment_1_d), .e(segment_1_e), .f(segment_1_f), .g(segment_1_g));
  TEN_S_segment ten_s_segment_1 (
    .B(multiplexer_3_out[1]), .C(multiplexer_3_out[2]), .D(multiplexer_3_out[3]), .E(multiplexer_3_out[4]),
    .a(ten_s_segment_1_a), .b_2(ten_s_segment_1_b_2), .c_2(ten_s_segment_1_c_2), .d_2(ten_s_segment_1_d_2),
    .e_2(ten_s_segment_1_e_2), .f(ten_s_segment_1_f), .g(ten_s_segment_1_g));
  and and_4 (and_4_out, OUTPUT[4], ~UNSIGNED);  // AND_Gate
  LED IS_NEGATIVE (.in(and_4_out));
  _7_Segment_Display u_7_segment_display_1 (
    .g(ten_s_segment_1_g), .f(ten_s_segment_1_f), .a(ten_s_segment_1_a), .b(ten_s_segment_1_b_2),
    .e(ten_s_segment_1_e_2), .d(ten_s_segment_1_d_2), .c(ten_s_segment_1_c_2));  // open: dp
  _7_Segment_Display u_7_segment_display_2 (
    .g(segment_1_g), .f(segment_1_f), .a(segment_1_a), .b(segment_1_b), .e(segment_1_e), .d(segment_1_d),
    .c(segment_1_c));  // open: dp
endmodule

module segment (
  input  A0,
  input  A1,
  input  A2,
  input  A3,
  input  A4,
  output a,
  output b,
  output c,
  output d,
  output e,
  output f,
  output g
);

  wire adder_1_cout, adder_1_out, adder_2_cout, adder_2_out, adder_3_cout, adder_3_out, adder_4_out,
       and_1_out, and_2_out, and_3_out, and_4_out, and_5_out, and_6_out, and_7_out, and_8_out, and_9_out,
       and_10_out, and_11_out, and_12_out, and_13_out, and_14_out, and_15_out, and_16_out, and_17_out,
       and_18_out, and_19_out, and_20_out, and_21_out, and_22_out, and_23_out, and_24_out, not_1_out,
       not_2_out, not_3_out, not_4_out, not_5_out, not_6_out, not_7_out, or_1_out, or_2_out, or_3_out,
       or_5_out, xnor_1_out, xnor_2_out, xor_1_out, xor_2_out, xor_3_out, xor_4_out;

  not not_1 (not_1_out, A1);
  and and_1 (and_1_out, not_1_out, A2, A3, A4, A2);
  not not_2 (not_2_out, A2);
  not not_3 (not_3_out, A3);
  xor xor_1 (xor_1_out, A2, A3);
  and and_2 (and_2_out, not_2_out, not_3_out, A4);
  and and_3 (and_3_out, A4, A3, A2, A1);
  or or_1 (or_1_out, and_1_out, and_4_out);
  and and_4 (and_4_out, xor_1_out, A4);
  or or_2 (or_2_out, and_2_out, and_3_out);
  or or_3 (or_3_out, and_2_out, or_1_out, or_1_out);
  Adder #(.width(1)) adder_1 (.a(A0), .b(1'b0), .out(adder_1_out), .cout(adder_1_cout));  // open: cin
  Adder #(.width(1)) adder_2 (.a(A1), .b(or_2_out), .out(adder_2_out), .cin(adder_1_cout), .cout(adder_2_cout));
  Adder #(.width(1)) adder_3 (.a(A2), .b(or_3_out), .out(adder_3_out), .cin(adder_2_cout), .cout(adder_3_cout));
  Adder #(.width(1)) adder_4 (.a(A3), .b(or_1_out), .out(adder_4_out), .cin(adder_3_cout));  // open: cout
  xor xor_2 (xor_2_out, adder_3_out, adder_4_out);
  not not_4 (not_4_out, adder_4_out);
  not not_5 (not_5_out, adder_3_out);
  not not_6 (not_6_out, adder_2_out);
  not not_7 (not_7_out, adder_1_out);
  xor xor_3 (xor_3_out, adder_2_out, adder_4_out);
  xnor xnor_1 (xnor_1_out, adder_1_out, adder_3_out);
  xnor xnor_2 (xnor_2_out, adder_3_out, adder_2_out);
  or or_4 (a, xor_3_out, xnor_1_out);
  xor xor_4 (xor_4_out, adder_2_out, adder_4_out);
  and and_5 (and_5_out, not_4_out, adder_2_out, adder_1_out);
  and and_6 (and_6_out, not_5_out, adder_4_out);
  and and_7 (and_7_out, not_7_out, not_4_out, adder_2_out);
  and and_8 (and_8_out, adder_4_out, adder_3_out, adder_1_out);
  and and_9 (and_9_out, not_5_out, not_4_out, adder_2_out);
  and and_10 (and_10_out, not_5_out, not_7_out);
  or or_5 (or_5_out, not_7_out, adder_3_out);
  and and_11 (and_11_out, adder_4_out, adder_3_out);
  and and_12 (and_12_out, adder_3_out, not_6_out);
  and and_13 (and_13_out, not_6_out, not_7_out);
  and and_14 (and_14_out, not_6_out, adder_4_out);
  and and_15 (and_15_out, adder_4_out, not_7_out);
  and and_16 (and_16_out, not_6_out, not_4_out);
  and and_17 (and_17_out, adder_2_out, adder_3_out);
  and and_18 (and_18_out, not_6_out, adder_1_out, adder_3_out);
  or or_6 (e, and_10_out, and_19_out);
  and and_19 (and_19_out, not_7_out, xor_4_out);
  and and_20 (and_20_out, not_7_out, xnor_2_out);
  and and_21 (and_21_out, not_6_out, xor_2_out);
  and and_22 (and_22_out, not_4_out, not_5_out, adder_2_out);
  and and_23 (and_23_out, not_7_out, adder_3_out);
  or or_7 (b, and_13_out, not_5_out, and_14_out, and_5_out, and_15_out);
  or or_8 (c, and_6_out, and_16_out, and_17_out, adder_1_out);
  and and_24 (and_24_out, or_5_out, adder_4_out, adder_2_out);
  or or_9 (d, and_7_out, and_14_out, and_18_out, and_8_out, and_9_out, and_10_out);
  or or_10 (f, and_20_out, and_21_out, and_24_out);
  or or_11 (g, and_14_out, and_22_out, and_11_out, and_12_out, and_23_out);
endmodule

module TEN_S_segment (
  input  B,
  input  C,
  input  D,
  input  E,
  output a,
  output b_2,
  output c_2,
  output d_2,
  output e_2,
  output f,
  output g
);

  wire and_1_out, and_2_out, and_3_out, and_4_out, and_5_out, and_6_out, and_7_out, and_8_out, and_9_out,
       and_10_out, and_11_out, and_12_out, and_13_out, E_XNOR_D_out, not_1_out, not_2_out, not_3_out,
       not_4_out;

  or or_1 (b_2, ~E, E);  // OR_Gate
  and and_1 (and_1_out, C, E);
  and and_2 (and_2_out, B, D, C);
  and and_3 (and_3_out, D, ~C, ~B);  // AND_Gate
  and and_4 (and_4_out, E, C, ~B);  // AND_Gate
  and and_5 (and_5_out, E, D, ~C);  // AND_Gate
  and and_6 (and_6_out, ~E, ~D);  // AND_Gate
  and and_7 (and_7_out, C, ~D);  // AND_Gate
  and and_8 (and_8_out, ~E, ~C, ~B);  // AND_Gate
  and and_9 (and_9_out, ~E, ~D);  // AND_Gate
  and and_10 (and_10_out, E, D);
  and and_11 (and_11_out, E, C);
  not not_1 (not_1_out, E);
  not not_2 (not_2_out, D);
  not not_3 (not_3_out, C);
  not not_4 (not_4_out, B);
  or or_2 (f, and_8_out, and_9_out);
  xnor E_XNOR_D (E_XNOR_D_out, D, E);
  or or_3 (e_2, and_3_out, and_4_out, and_5_out, and_6_out, and_7_out);
  or or_4 (g, and_10_out, and_11_out);
  and and_12 (and_12_out, not_1_out, not_4_out, not_3_out);
  and and_13 (and_13_out, not_3_out, not_2_out);
  or or_5 (c_2, not_1_out, and_13_out, and_2_out);
  or or_6 (a, and_1_out, E_XNOR_D_out, and_12_out);
  _7_Segment_Display u_7_segment_display_1 (.g(g), .f(f), .a(a), .b(b_2), .e(e_2), .d(a), .c(c_2));  // open: dp

  assign d_2 = a;
endmodule

module _2_4_DECODER (
  input  A,
  input  B,
  output out_3,
  output out_4,
  output out_5,
  output out_6
);

  and and_1 (out_3, ~A, ~B);  // AND_Gate
  and and_2 (out_4, A, ~B);  // AND_Gate
  and and_3 (out_5, ~A, B);  // AND_Gate
  and and_4 (out_6, A, B);
endmodule

module _2_S_COMP_SEGMENT (
  input  _2_S_COMP,
  input  UNSIGNED,
  output F,
  output CARRY_CHANGER
);

  and and_1 (F, _2_S_COMP, ~UNSIGNED);  // AND_Gate
  not not_1 (CARRY_CHANGER, UNSIGNED);
endmodule

module negator (
  input  [4:0] in_1,
  output [4:0] F
);

  wire adder_1_cout, adder_2_cout, adder_3_cout, xor_1_out, xor_2_out, xor_3_out, xor_4_out;

  xor xor_1 (xor_1_out, in_1[0], in_1[4]);
  Adder #(.width(1)) adder_1 (.a(xor_1_out), .b(1'b0), .out(F[0]), .cin(in_1[4]), .cout(adder_1_cout));
  xor xor_2 (xor_2_out, in_1[1], in_1[4]);
  Adder #(.width(1)) adder_2 (.a(xor_2_out), .b(1'b0), .out(F[1]), .cin(adder_1_cout), .cout(adder_2_cout));
  xor xor_3 (xor_3_out, in_1[2], in_1[4]);
  Adder #(.width(1)) adder_3 (.a(xor_3_out), .b(1'b0), .out(F[2]), .cin(adder_2_cout), .cout(adder_3_cout));
  xor xor_4 (xor_4_out, in_1[3], in_1[4]);
  Adder #(.width(1)) adder_4 (.a(xor_4_out), .b(1'b0), .out(F[3]), .cin(adder_3_cout), .cout(F[4]));
endmodule
